// Logisim project additionneurs.circ as structural Verilog: 7 circuits, main circuit incrementation 3 bits
module additionneur_3bits_optimise (
  input  retenue,
  input  [2:0] x,
  input  [2:0] y,
  output [2:0] x_y_retenue,
  output Retenue_2
);

  wire additionneur_1b_optimise_1_genere, additionneur_1b_optimise_1_propage,
       additionneur_1b_optimise_2_genere, additionneur_1b_optimise_2_propage,
       additionneur_1b_optimise_3_genere, additionneur_1b_optimise_3_propage, and_1_out, and_2_out,
       and_3_out, and_4_out, and_5_out, and_6_out, or_1_out, or_2_out, or_3_out, or_4_out, or_5_out;

  additionneur_1b_optimise additionneur_1b_optimise_1 (
    .retenue(retenue), .x(x[0]), .y(y[0]), .x_y(x_y_retenue[0]),
    .propage(additionneur_1b_optimise_1_propage), .genere(additionneur_1b_optimise_1_genere));
  additionneur_1b_optimise additionneur_1b_optimise_2 (
    .retenue(or_1_out), .x(x[1]), .y(y[1]), .x_y(x_y_retenue[1]),
    .propage(additionneur_1b_optimise_2_propage), .genere(additionneur_1b_optimise_2_genere));
  and and_1 (and_1_out, additionneur_1b_optimise_1_propage, retenue);
  additionneur_1b_optimise additionneur_1b_optimise_3 (
    .retenue(or_3_out), .x(x[2]), .y(y[2]), .x_y(x_y_retenue[2]),
    .propage(additionneur_1b_optimise_3_propage), .genere(additionneur_1b_optimise_3_genere));
  or or_1 (or_1_out, additionneur_1b_optimise_1_genere, and_1_out);
  and and_2 (and_2_out, and_1_out, additionneur_1b_optimise_2_propage);
  and and_3 (and_3_out, additionneur_1b_optimise_1_genere, additionneur_1b_optimise_2_propage);
  or or_2 (or_2_out, and_2_out, and_3_out);
  and and_4 (and_4_out, and_2_out, additionneur_1b_optimise_3_propage);
  and and_5 (and_5_out, and_3_out, additionneur_1b_optimise_3_propage);
  and and_6 (and_6_out, additionneur_1b_optimise_2_genere, additionneur_1b_optimise_3_propage);
  or or_3 (or_3_out, or_2_out, additionneur_1b_optimise_2_genere);
  or or_4 (or_4_out, and_4_out, and_5_out);
  or or_5 (or_5_out, and_6_out, additionneur_1b_optimise_3_genere);
  or or_6 (Retenue_2, or_4_out, or_5_out);

  // Notes on the sheet:
  //   PrÃ©diction de retenue. 24 portes
endmodule

module incrementation_3_bits (
  input  retenue,
  input  [2:0] x,
  output [2:0] x_retenue,
  output Retenue_2
);

  wire additionneur_retenue_1b_1_propage, additionneur_retenue_1b_2_propage,
       additionneur_retenue_1b_3_propage, and_1_out, and_2_out;

  additionneur_retenue_1b additionneur_retenue_1b_1 (
    .retenue(retenue), .x(x[0]), .x_y(x_retenue[0]), .propage(additionneur_retenue_1b_1_propage));
  additionneur_retenue_1b additionneur_retenue_1b_2 (
    .retenue(and_1_out), .x(x[1]), .x_y(x_retenue[1]), .propage(additionneur_retenue_1b_2_propage));
  and and_1 (and_1_out, additionneur_retenue_1b_1_propage, retenue);
  additionneur_retenue_1b additionneur_retenue_1b_3 (
    .retenue(and_2_out), .x(x[2]), .x_y(x_retenue[2]), .propage(additionneur_retenue_1b_3_propage));
  and and_2 (and_2_out, and_1_out, additionneur_retenue_1b_2_propage);
  and and_3 (Retenue_2, and_2_out, additionneur_retenue_1b_3_propage);

  // Notes on the sheet:
  //   N'additionne que la retenue. 6 portes
endmodule

module additionneur_1b_optimise (
  input  retenue,
  input  x,
  input  y,
  output x_y,
  output propage,
  output genere
);

  wire xor_1_out;

  xor xor_1 (xor_1_out, retenue, x);
  xor xor_2 (x_y, xor_1_out, y);
  or or_1 (propage, x, y);
  and and_1 (genere, x, y);
endmodule

module additionneur_retenue_1b (
  input  retenue,
  input  x,
  output x_y,
  output propage
);

  xor xor_1 (x_y, retenue, x);

  assign propage = x;
endmodule

module decrementeur_3bits (
  input  \annule_dÃ_crÃ_mentation ,
  input  [2:0] x,
  output [2:0] x_y_retenue,
  output Overflow
);

  wire decrementeur_1b_optimise_1_genere, decrementeur_1b_optimise_2_genere,
       decrementeur_1b_optimise_3_genere, or_1_out, or_2_out, or_3_out, or_4_out, or_5_out;

  decrementeur_1b_optimise decrementeur_1b_optimise_1 (
    .retenue(\annule_dÃ_crÃ_mentation ), .x(x[0]), .x_y(x_y_retenue[0]),
    .genere(decrementeur_1b_optimise_1_genere));
  decrementeur_1b_optimise decrementeur_1b_optimise_2 (
    .retenue(or_1_out), .x(x[1]), .x_y(x_y_retenue[1]), .genere(decrementeur_1b_optimise_2_genere));
  decrementeur_1b_optimise decrementeur_1b_optimise_3 (
    .retenue(or_3_out), .x(x[2]), .x_y(x_y_retenue[2]), .genere(decrementeur_1b_optimise_3_genere));
  or or_1 (or_1_out, decrementeur_1b_optimise_1_genere, \annule_dÃ_crÃ_mentation );
  or or_2 (or_2_out, \annule_dÃ_crÃ_mentation , decrementeur_1b_optimise_1_genere);
  or or_3 (or_3_out, or_2_out, decrementeur_1b_optimise_2_genere);
  or or_4 (or_4_out, \annule_dÃ_crÃ_mentation , decrementeur_1b_optimise_1_genere);
  or or_5 (or_5_out, decrementeur_1b_optimise_2_genere, decrementeur_1b_optimise_3_genere);
  nor nor_1 (Overflow, or_4_out, or_5_out);

  // Notes on the sheet:
  //   DÃ©crÃ©menteur Ã  prÃ©diction de retenue. 9 portes
endmodule

module decrementeur_1b_optimise (
  input  retenue,
  input  x,
  output x_y,
  output genere
);

  xnor xnor_1 (x_y, retenue, x);

  assign genere = x;
endmodule

module alu (
  input  Overflow,
  input  Ignore_overflow,
  input  _1_si_NOT__0_si_INC_DEC,
  input  _1_si_INC__0_si_DEC,
  input  [2:0] in,
  output Overflow_out,
  output [2:0] out,
  output Zero_Flag_out
);

  wire and_1_out, and_2_out, and_3_out, \DÃ_crÃ_menteur_overflow , \IncrÃ_menteur_retenue_2 , nand_1_out,
       nor_1_out, nor_2_out, or_1_out, or_2_out;
  wire [0:0] xor_1_out;
  wire [2:0] \DÃ_crÃ_menteur_x_y_retenue , \IncrÃ_menteur_x_retenue ;

  nor nor_1 (nor_1_out, Overflow, Ignore_overflow);
  or or_1 (or_1_out, Overflow, Ignore_overflow);
  and and_1 (and_1_out, or_1_out, _1_si_NOT__0_si_INC_DEC);
  and and_2 (and_2_out, _1_si_NOT__0_si_INC_DEC, Ignore_overflow);
  nand nand_1 (nand_1_out, or_1_out, _1_si_NOT__0_si_INC_DEC);
  xor xor_1 (xor_1_out[0], and_2_out, in[0]);
  nor nor_2 (nor_2_out, _1_si_INC__0_si_DEC, and_1_out);
  and and_3 (and_3_out, _1_si_INC__0_si_DEC, nand_1_out);
  incrementation_3_bits \IncrÃ_menteur  (
    .retenue(or_1_out), .x(in), .x_retenue(\IncrÃ_menteur_x_retenue ), .Retenue_2(\IncrÃ_menteur_retenue_2 ));
  decrementeur_3bits \DÃ_crÃ_menteur  (
    .\annule_dÃ_crÃ_mentation (nor_1_out), .x(in), .x_y_retenue(\DÃ_crÃ_menteur_x_y_retenue ),
    .Overflow(\DÃ_crÃ_menteur_overflow ));
  or or_2 (or_2_out, in[1], in[0]);
  Transistor #(.\type ("n")) transistor_1 (.in(\DÃ_crÃ_menteur_overflow ), .out(Overflow_out), .gate(nor_2_out));
  Transistor #(.\type ("n"), .width(3)) transistor_2 (.in(\DÃ_crÃ_menteur_x_y_retenue ), .out(out), .gate(nor_2_out));
  nor nor_3 (Zero_Flag_out, or_2_out, in[2]);
  Transistor #(.\type ("n")) transistor_3 (.in(\IncrÃ_menteur_retenue_2 ), .out(Overflow_out), .gate(and_3_out));
  Transistor #(.\type ("n"), .width(3)) transistor_4 (.in(\IncrÃ_menteur_x_retenue ), .out(out), .gate(and_3_out));
  Transistor #(.\type ("n"), .width(3)) transistor_5 (.in({in[2:1], xor_1_out[0]}), .out(out), .gate(and_1_out));
endmodule
