// Logisim project timer.circ as structural Verilog: 1 circuit, main circuit compteur 10bits
module compteur_10bits (
  input  CLK,
  input  On,
  input  Reset,
  output TIMER_INTERRUPTION
);

  wire additionneur_retenue_1b_1_propage, incrementation_3_bits_1_retenue_2,
       incrementation_3_bits_2_retenue_2, incrementation_3_bits_3_retenue_2;
  wire [4:0] incrementation_3_bits_2_x_retenue, incrementation_3_bits_3_x_retenue, registre_5b_reset_1_out_5,
       registre_5b_reset_2_out_5;

  registre_5b_reset registre_5b_reset_1 (
    .in_4(incrementation_3_bits_2_x_retenue), .out_5(registre_5b_reset_1_out_5), .Reset(Reset),
    .Ecriture(On), .Lecture(CLK));
  registre_5b_reset registre_5b_reset_2 (
    .in_4(incrementation_3_bits_3_x_retenue), .out_5(registre_5b_reset_2_out_5), .Reset(Reset),
    .Ecriture(On), .Lecture(CLK));
  incrementation_3_bits incrementation_3_bits_1 (
    .retenue(On), .x(registre_5b_reset_1_out_5[2:0]), .x_retenue(incrementation_3_bits_2_x_retenue[2:0]),
    .Retenue_2(incrementation_3_bits_1_retenue_2));
  incrementation_3_bits incrementation_3_bits_2 (
    .retenue(incrementation_3_bits_1_retenue_2),
    .x({registre_5b_reset_2_out_5[0], registre_5b_reset_1_out_5[4:3]}),
    .x_retenue({incrementation_3_bits_3_x_retenue[0], incrementation_3_bits_2_x_retenue[4:3]}),
    .Retenue_2(incrementation_3_bits_2_retenue_2));
  incrementation_3_bits incrementation_3_bits_3 (
    .retenue(incrementation_3_bits_2_retenue_2), .x(registre_5b_reset_2_out_5[3:1]),
    .x_retenue(incrementation_3_bits_3_x_retenue[3:1]), .Retenue_2(incrementation_3_bits_3_retenue_2));
  additionneur_retenue_1b additionneur_retenue_1b_1 (
    .retenue(incrementation_3_bits_3_retenue_2), .x(registre_5b_reset_2_out_5[4]),
    .x_y(incrementation_3_bits_3_x_retenue[4]), .propage(additionneur_retenue_1b_1_propage));
  and and_1 (TIMER_INTERRUPTION, additionneur_retenue_1b_1_propage, incrementation_3_bits_3_retenue_2);
endmodule
